// Logisim project cpu_design.circ as structural Verilog: 2 circuits, main circuit main
module main (
  input  [7:0] in_1,
  input  [7:0] in_2,
  input  in_3
);

  wire clock_1_out;

  Register register_1 (.D(in_2), .en(in_3), .Q(in_1), .clk(clock_1_out));  // open: clr
  Clock clock_1 (.out(clock_1_out));

  // Notes on the sheet:
  //   register a
endmodule

// output
module AU (
  input  [7:0] input_b,
  input  [7:0] input_a,
  input  mode_sub_add,
  output out_4,
  output z_flag,
  output [7:0] \output 
);

  wire [7:0] bit_extender_1_out, xor_1_out;

  assign bit_extender_1_out = {{7{1'b1}}, mode_sub_add};  // Bit_Extender bit_extender_1
  assign xor_1_out = input_b ^ bit_extender_1_out;  // XOR_Gate xor_1, 8 bits wide
  Adder adder_1 (.a(input_a), .b(xor_1_out), .out(\output ), .cin(mode_sub_add), .cout(out_4));
  Comparator comparator_1 (.a(\output ), .b({8{1'b0}}), .eq(z_flag));  // open: gt, lt
endmodule
